// Logisim project ATTEMPT - 32BIT CPU INCOMPLETE.circ as structural Verilog: 10 circuits, main circuit ADD 8BIT
module ADD_8BIT (
  input  in_1,
  input  [7:0] in_2,
  input  [7:0] in_3,
  output [7:0] out_4,
  output out_5
);

  wire adder_1_cout, adder_2_cout, adder_3_cout, adder_4_cout, adder_5_cout, adder_6_cout, adder_7_cout;

  Adder #(.width(1)) adder_1 (.a(in_2[0]), .b(in_3[0]), .out(out_4[0]), .cin(in_1), .cout(adder_1_cout));
  Adder #(.width(1)) adder_2 (.a(in_2[1]), .b(in_3[1]), .out(out_4[1]), .cin(adder_1_cout), .cout(adder_2_cout));
  Adder #(.width(1)) adder_3 (.a(in_2[2]), .b(in_3[2]), .out(out_4[2]), .cin(adder_2_cout), .cout(adder_3_cout));
  Adder #(.width(1)) adder_4 (.a(in_2[3]), .b(in_3[3]), .out(out_4[3]), .cin(adder_3_cout), .cout(adder_4_cout));
  Adder #(.width(1)) adder_5 (.a(in_2[4]), .b(in_3[4]), .out(out_4[4]), .cin(adder_4_cout), .cout(adder_5_cout));
  Adder #(.width(1)) adder_6 (.a(in_2[5]), .b(in_3[5]), .out(out_4[5]), .cin(adder_5_cout), .cout(adder_6_cout));
  Adder #(.width(1)) adder_7 (.a(in_2[6]), .b(in_3[6]), .out(out_4[6]), .cin(adder_6_cout), .cout(adder_7_cout));
  Adder #(.width(1)) adder_8 (.a(in_2[7]), .b(in_3[7]), .out(out_4[7]), .cin(adder_7_cout), .cout(out_5));
endmodule

module ADD_32BIT (
  input  [31:0] in_1,
  input  [31:0] in_2,
  output [31:0] out_3
);

  wire add_8bit_1_out_5, add_8bit_2_out_5, add_8bit_3_out_5, add_8bit_4_out_5;
  wire [7:0] add_8bit_3_out_4;
  wire [31:0] add_8bit_1_out_4, bit_extender_1_out;

  ADD_8BIT add_8bit_1 (
    .in_2(in_1[7:0]), .in_3(in_2[7:0]), .out_4(add_8bit_1_out_4[7:0]), .out_5(add_8bit_1_out_5));  // open: in_1
  ADD_8BIT add_8bit_2 (
    .in_2(in_1[15:8]), .in_3(in_2[15:8]), .out_4(add_8bit_1_out_4[15:8]), .in_1(add_8bit_1_out_5),
    .out_5(add_8bit_2_out_5));
  ADD_8BIT add_8bit_3 (
    .in_2(in_1[23:16]), .in_3(in_2[23:16]), .out_4(add_8bit_3_out_4), .in_1(add_8bit_2_out_5),
    .out_5(add_8bit_3_out_5));
  ADD_8BIT add_8bit_4 (
    .in_2(in_1[31:24]), .in_3(in_2[31:24]), .out_4(add_8bit_1_out_4[31:24]), .in_1(add_8bit_3_out_5),
    .out_5(add_8bit_4_out_5));
  assign bit_extender_1_out = {{31{1'b0}}, add_8bit_4_out_5};  // Bit_Extender bit_extender_1
  Adder #(.width(32)) adder_1 (
    .a({add_8bit_1_out_4[31:24], add_8bit_3_out_4, add_8bit_1_out_4[15:0]}), .b(bit_extender_1_out),
    .out(out_3));  // open: cin, cout
endmodule

module SUB_8BIT (
  input  in_1,
  input  [7:0] in_2,
  input  [7:0] in_3,
  output [7:0] out_4,
  output out_5
);

  wire subtractor_1_bout, subtractor_2_bout, subtractor_3_bout, subtractor_4_bout, subtractor_5_bout,
       subtractor_6_bout, subtractor_7_bout;

  Subtractor #(.width(1)) subtractor_1 (.a(in_2[0]), .b(in_3[0]), .out(out_4[0]), .bin(in_1), .bout(subtractor_1_bout));
  Subtractor #(.width(1)) subtractor_2 (
    .a(in_2[1]), .b(in_3[1]), .out(out_4[1]), .bin(subtractor_1_bout), .bout(subtractor_2_bout));
  Subtractor #(.width(1)) subtractor_3 (
    .a(in_2[2]), .b(in_3[2]), .out(out_4[2]), .bin(subtractor_2_bout), .bout(subtractor_3_bout));
  Subtractor #(.width(1)) subtractor_4 (
    .a(in_2[3]), .b(in_3[3]), .out(out_4[3]), .bin(subtractor_3_bout), .bout(subtractor_4_bout));
  Subtractor #(.width(1)) subtractor_5 (
    .a(in_2[4]), .b(in_3[4]), .out(out_4[4]), .bin(subtractor_4_bout), .bout(subtractor_5_bout));
  Subtractor #(.width(1)) subtractor_6 (
    .a(in_2[5]), .b(in_3[5]), .out(out_4[5]), .bin(subtractor_5_bout), .bout(subtractor_6_bout));
  Subtractor #(.width(1)) subtractor_7 (
    .a(in_2[6]), .b(in_3[6]), .out(out_4[6]), .bin(subtractor_6_bout), .bout(subtractor_7_bout));
  Subtractor #(.width(1)) subtractor_8 (
    .a(in_2[7]), .b(in_3[7]), .out(out_4[7]), .bin(subtractor_7_bout), .bout(out_5));
endmodule

module SUB_32BIT (
  input  [31:0] in_1,
  input  [31:0] in_2,
  output [31:0] out_3,
  output out_4
);

  wire sub_8bit_1_out_5, sub_8bit_2_out_5, sub_8bit_3_out_5;

  SUB_8BIT sub_8bit_1 (.in_2(in_1[7:0]), .in_3(in_2[7:0]), .out_4(out_3[7:0]), .out_5(sub_8bit_1_out_5));  // open: in_1
  SUB_8BIT sub_8bit_2 (
    .in_2(in_1[15:8]), .in_3(in_2[15:8]), .out_4(out_3[15:8]), .in_1(sub_8bit_1_out_5),
    .out_5(sub_8bit_2_out_5));
  SUB_8BIT sub_8bit_3 (
    .in_2(in_1[23:16]), .in_3(in_2[23:16]), .out_4(out_3[23:16]), .in_1(sub_8bit_2_out_5),
    .out_5(sub_8bit_3_out_5));
  SUB_8BIT sub_8bit_4 (
    .in_2(in_1[31:24]), .in_3(in_2[31:24]), .out_4(out_3[31:24]), .in_1(sub_8bit_3_out_5), .out_5(out_4));
endmodule

module MUL_32BIT (
  input  [31:0] in_1,
  input  [31:0] in_2,
  input  [31:0] in_3,
  output [31:0] out_4,
  output [31:0] out_5
);

  Multiplier #(.width(32)) multiplier_1 (.a(in_2), .b(in_3), .out(out_4), .cin(in_1), .cout(out_5));
endmodule

module DIV_32BIT (
  input  [31:0] in_1,
  input  [31:0] in_2,
  output [31:0] out_3,
  output [31:0] out_4
);

  Divider #(.width(32)) divider_1 (.a(in_1), .b(in_2), .out(out_3), .rem(out_4));  // open: upper
endmodule

module ALU_32BIT (
  input  [31:0] in_1,
  input  [31:0] in_2,
  input  [31:0] MUL_OVERFLOW,
  input  [31:0] remainder,
  input  [1:0] in_5,
  output [31:0] out_6
);

  wire [31:0] add_32bit_1_out_3, demultiplexer_1_out0, demultiplexer_1_out1, demultiplexer_1_out2,
       demultiplexer_1_out3, demultiplexer_2_out0, demultiplexer_2_out1, demultiplexer_2_out2,
       demultiplexer_2_out3, div_32bit_1_out_3, mul_32bit_1_out_4, sub_32bit_1_out_3;

  Demultiplexer #(.select(2), .width(32)) demultiplexer_1 (
    .out0(demultiplexer_1_out0), .out1(demultiplexer_1_out1), .out2(demultiplexer_1_out2),
    .out3(demultiplexer_1_out3), .in(in_1), .sel(in_5));  // open: en
  Demultiplexer #(.select(2), .width(32)) demultiplexer_2 (
    .out0(demultiplexer_2_out0), .out1(demultiplexer_2_out1), .out2(demultiplexer_2_out2),
    .out3(demultiplexer_2_out3), .in(in_2), .sel(in_5));  // open: en
  ADD_32BIT add_32bit_1 (.in_1(demultiplexer_1_out0), .in_2(demultiplexer_2_out0), .out_3(add_32bit_1_out_3));
  SUB_32BIT sub_32bit_1 (
    .in_1(demultiplexer_1_out1), .in_2(demultiplexer_2_out1), .out_3(sub_32bit_1_out_3));  // open: out_4
  MUL_32BIT mul_32bit_1 (
    .in_2(demultiplexer_1_out2), .in_3(demultiplexer_2_out2), .out_4(mul_32bit_1_out_4), .out_5(MUL_OVERFLOW));  // open: in_1
  DIV_32BIT div_32bit_1 (
    .in_1(demultiplexer_1_out3), .in_2(demultiplexer_2_out3), .out_3(div_32bit_1_out_3), .out_4(remainder));
  Multiplexer #(.select(2), .width(32)) multiplexer_1 (
    .in0(add_32bit_1_out_3), .in1(sub_32bit_1_out_3), .in2(mul_32bit_1_out_4), .in3(div_32bit_1_out_3),
    .out(out_6), .sel(in_5));  // open: en
endmodule

// JMP REGISTER
module REG_32BIT (
  input  [31:0] in_1,
  output [31:0] out_2
);

  wire clock_1_out;

  Clock clock_1 (.out(clock_1_out));
  Register register_1 (.D(in_1[7:0]), .Q(out_2[7:0]), .clk(clock_1_out));  // open: en, clr
  Register register_2 (.D(in_1[15:8]), .Q(out_2[15:8]), .clk(clock_1_out));  // open: en, clr
  Register register_3 (.D(in_1[23:16]), .Q(out_2[23:16]), .clk(clock_1_out));  // open: en, clr
  Register register_4 (.D(in_1[31:24]), .Q(out_2[31:24]), .clk(clock_1_out));  // open: en, clr
endmodule

module MAR (
  input  [31:0] in_1,
  input  in_2,
  input  in_3,
  output [31:0] out_4
);

  wire [31:0] register_1_q;

  Register register_1 (.D(in_1[7:0]), .Q(register_1_q[7:0]), .clk(in_2));  // open: en, clr
  Register register_2 (.D(in_1[15:8]), .Q(register_1_q[15:8]), .clk(in_2));  // open: en, clr
  Register register_3 (.D(in_1[23:16]), .Q(register_1_q[23:16]), .clk(in_2));  // open: en, clr
  Register register_4 (.D(in_1[31:24]), .Q(register_1_q[31:24]), .clk(in_2));  // open: en, clr
  assign out_4 = in_3 ? register_1_q : 32'bz;  // Controlled_Buffer controlled_buffer_1
endmodule

module main (
  input  [31:0] in_1,
  input  [31:0] in_2,
  input  Reset_Counter,
  input  [7:0] Instruction_Address_To_Jump,
  output [31:0] out_5,
  output [31:0] out_6
);

  wire and_1_out, and_2_out, clock_1_out, not_1_out, not_2_out, not_3_out, not_4_out, or_1_out;
  wire [1:0] controlled_buffer_1_out;
  wire [7:0] Program_Counter_q, register_1_q;
  wire [15:0] rom_1_data;

  REG_32BIT REG_A (.in_1(in_1));  // open: out_2
  REG_32BIT REG_B (.in_1(in_2));  // open: out_2
  Counter Program_Counter (.Q(Program_Counter_q), .clk(clock_1_out), .clr(or_1_out));  // open: load, D, count, carry
  or or_1 (or_1_out, Reset_Counter, and_2_out);
  Register register_1 (.D(Program_Counter_q), .Q(register_1_q), .clk(clock_1_out));  // open: en, clr
  Clock clock_1 (.out(clock_1_out));
  ROM #(.dataWidth(16)) rom_1 (.addr(register_1_q), .data(rom_1_data));  // open: sel
  ALU_32BIT alu_32bit_1 (
    .in_1(in_1), .in_2(in_2), .out_6(out_5), .in_5(controlled_buffer_1_out), .remainder(out_6));  // open: MUL_OVERFLOW
  REG_32BIT REG_C (.in_1(out_5));  // open: out_2
  assign controlled_buffer_1_out = and_1_out ? {rom_1_data[4], rom_1_data[0]} : 2'bz;  // Controlled_Buffer controlled_buffer_1
  and and_1 (and_1_out, rom_1_data[8], rom_1_data[12]);
  not not_1 (not_1_out, rom_1_data[12]);
  not not_2 (not_2_out, rom_1_data[4]);
  and and_2 (and_2_out, not_2_out, rom_1_data[8], rom_1_data[0], not_1_out);
  Hex_Digit_Display hex_digit_display_1 (.value(out_5[27:24]));  // open: dp
  Hex_Digit_Display hex_digit_display_2 (.value(out_5[31:28]));  // open: dp
  not not_3 (not_3_out, rom_1_data[8]);
  not not_4 (not_4_out, rom_1_data[0]);
  Hex_Digit_Display hex_digit_display_3 (.value(out_5[19:16]));  // open: dp
  Hex_Digit_Display hex_digit_display_4 (.value(out_5[23:20]));  // open: dp
  Register register_2 (.D(Instruction_Address_To_Jump), .clk(clock_1_out));  // open: en, Q, clr
  // AND_Gate and_3 has open pins: in1=not_3_out, in2=rom_1_data[12], in3=rom_1_data[4], out=open
  Hex_Digit_Display hex_digit_display_5 (.value(out_5[11:8]));  // open: dp
  Hex_Digit_Display hex_digit_display_6 (.value(out_5[15:12]));  // open: dp
  Hex_Digit_Display hex_digit_display_7 ();  // open: value, dp
  Hex_Digit_Display hex_digit_display_8 (.value(out_5[7:4]));  // open: dp

  // Notes on the sheet:
  //   !!!!!
  //   contents of rom_1 (hex, n*v repeats v):
  //   0 1100 1101 1110 1111 0 0 0 1010 101
  //   !!!!!
  //   !!!!!
  //   !!!!!
  //   !!!!!
  //   !!!!!
endmodule
