// Logisim project Generating,Storing and Displaying Random Numbers Machine (TURING INCOMPLETE).circ as structural Verilog: 1 circuit, main circuit main
module main (
  input  in_1,
  input  in_2,
  input  Stop_Button
);

  wire button_1_out, button_2_out, clock_1_out, transistor_1_out, transistor_2_out;
  wire [3:0] transistor_3_out, transistor_3_out_2;
  wire [7:0] bit_extender_1_out, counter_1_q, ram_1_data, random_1_out;

  Clock clock_1 (.out(clock_1_out));
  Transistor #(.gate("br")) transistor_1 (.in(clock_1_out), .out(transistor_1_out), .gate(Stop_Button));
  Counter counter_1 (.Q(counter_1_q), .clk(transistor_1_out), .clr(button_1_out));  // open: load, D, count, carry
  Transistor #(.\type ("n")) transistor_2 (.in(transistor_1_out), .out(transistor_2_out), .gate(in_1));
  Random random_1 (.clk(transistor_2_out), .out(random_1_out));  // open: next, clr
  Button button_1 (.out(button_1_out));
  Button button_2 (.out(button_2_out));
  RAM #(.bus("separate")) ram_1 (
    .addr(counter_1_q), .din(random_1_out), .data(ram_1_data), .clk(transistor_2_out), .clr(button_2_out));  // open: str, sel, ld
  Bit_Extender #(.out_width(8)) bit_extender_1 (.in(ram_1_data), .out(bit_extender_1_out));
  Transistor #(.\type ("n"), .gate("br"), .width(8)) transistor_3 (
    .in(bit_extender_1_out), .out({transistor_3_out_2, transistor_3_out}), .gate(in_2));
  Hex_Digit_Display hex_digit_display_1 (.value(transistor_3_out_2));  // open: dp
  Hex_Digit_Display hex_digit_display_2 (.value(transistor_3_out));  // open: dp

  // Notes on the sheet:
  //   Generate And Store MODE
  //   Reset Counter
  //   Reset Memory
  //   Read And Display MODE
endmodule
